# Fritzing sketch Prototype Design (saved by Fritzing 1.0.2b)
breadboards: 1

parts:
  Part1 = Arduino Uno (Rev3) - ICSP
  U1 = OBDII [package=obdii]
  M1 = RioRand LM2596
  SN65HVDA1 = TI SN65HVDA195 LIN Physical Interface IC [chip_label=SN65HVDA195 package="DIP (Dual Inline) [THT]"]
  D1 = Rectifier Diode [part_number=1N4001 package="300 mil [THT]"]
  C1 = Capacitor [package=cap-pth-small]
  D2 = Rectifier Diode [part_number=1N4001 package="300 mil [THT]"]
  R1 = Resistor [tolerance=±5% resistance=1k package="2512 [SMD]"]

nets:
  N1: Part1.D8, SN65HVDA1.pin1_(RXD)
  N2: Part1.D9_PWM, SN65HVDA1.pin4_(TXD)
  N3: Part1.D10_PWM/SS, SN65HVDA1.pin2_(EN)
  N4: Part1.GND, M1.Pin_4
  N5: Part1.VIN, M1.Pin_3
  N6: U1.CHASGND, M1.Pin_2, SN65HVDA1.pin3_(NWake), SN65HVDA1.pin5_(GND), C1.2
  N7: U1.ISOK-LINE, SN65HVDA1.pin6_(LIN), R1.Pin_1
  N8: U1.BATTPOWER, M1.Pin_1, D1.anode
  N9: SN65HVDA1.pin7_(Vsup), D1.cathode, C1.1, D2.anode
  N10: D2.cathode, R1.Pin_0

custom parts:
  TI SN65HVDA195 LIN Physical Interface IC: Local Interconnect Network (LIN) physical interface and MOST ECL interface, which integrates the serial transceiver with wake-up and protection features.
