# Fritzing sketch Prototype Design (saved by Fritzing 1.0.2b)
breadboards: 1

parts:
  Part1 = Arduino Uno (Rev3) - ICSP
  U1 = OBDII [package=obdii]
  M1 = RioRand LM2596

nets:
  N1: Part1.GND, M1.Pin_4
  N2: Part1.VIN, M1.Pin_3
  N3: U1.CHASGND, M1.Pin_2
  N4: U1.BATTPOWER, M1.Pin_1
